// Digital circuit ALU.dig as structural Verilog
module ALU (
  input  [7:0] inbus,
  input  [1:0] op,
  input  CLk,
  input  Begin,
  input  RST,
  output [7:0] outbus
);

  wire and_1_out, and_3_out, and_4_out, c0, c0_t, c1, c2, c3, c4, c6, c7, c8, cL, cnt7, cR, d_ff_1_q,
       d_ff_2_q, d_ff_3_q, d_ff_4_q, dir, O_SR, or_3_out, or_5_out, or_7_out, Q__1, r_shft, shft,
       shft_1_o_sl, shft_1_o_sr, shft_2_o_sl;
  wire [1:0] or_2_out;
  wire [7:0] A, driver_1_out, M_q, multiplexer_1_out, multiplexer_2_out, O_A, O_Q, Parallel_Adder_z, Q,
       xor_1_out;

  D_FF d_ff_1 (.D(shft), .C(CLk), .Q(d_ff_1_q));  // open: nQ
  or or_1 (or_2_out[1], c3, d_ff_1_q);
  or or_2 (or_2_out[0], c0_t, d_ff_1_q);
  or or_3 (or_3_out, c0, c0_t, c3, d_ff_1_q);
  // Probe on multiplexer_1_out
  Multiplexer #(.Selector_Bits(2), .Bits(8)) multiplexer_1 (
    .sel(or_2_out), .in_0({8{1'b0}}), .in_1(inbus), .in_2(Parallel_Adder_z), .in_3(O_A),
    .out(multiplexer_1_out));
  Register #(.Bits(8)) u_A (.D(multiplexer_1_out), .C(~CLk), .en(or_3_out), .Q(A));
  // Probe on A
  // Probe on A[6:0]
  D_FF d_ff_2 (.D(shft), .C(CLk), .Q(d_ff_2_q));  // open: nQ
  and and_1 (and_1_out, ~c1, d_ff_2_q);  // And
  and and_2 (dir, cL, ~cR);  // And
  or or_4 (shft, cL, cR);
  // Probe on multiplexer_2_out
  or or_5 (or_5_out, c1, d_ff_2_q);
  Multiplexer #(.Bits(8)) multiplexer_2 (.sel(and_1_out), .in_0(inbus), .in_1(O_Q), .out(multiplexer_2_out));
  Register #(.Bits(8)) u_Q (.D(multiplexer_2_out), .C(~CLk), .en(or_5_out), .Q(Q));
  ALU_CU alu_cu_1 (
    .BGN(Begin), .RST(RST), .CLK(CLk), .CNT7(cnt7), .Q0(Q[0]), .Q_1(Q__1), .A7(A[7]), .OP(op), .c0(c0),
    .c0_2(c0_t), .c1(c1), .c2(c2), .c3(c3), .c4(c4), .cR(cR), .cL(cL), .c7(c7), .c8(c8), .c6(c6));  // open: c5, c7_5
  // Probe on Q[0]
  // Probe on Q
  or or_6 (r_shft, RST, c3);
  // Probe on Q[7:1]
  or or_7 (or_7_out, c1, shft);
  and and_3 (and_3_out, r_shft, CLk);
  D_FF d_ff_3 (.D(c3), .C(~CLk), .Q(d_ff_3_q));  // open: nQ
  Register u_Q__1 (.D(O_SR), .C(~CLk), .en(or_7_out), .Q(Q__1));
  // Probe on Q__1
  SHFT shft_1 (
    .CLK(CLk), .DIR(dir), .IN_SR(A[7]), .IN_SL(shft_2_o_sl), .RST(and_3_out), .IN(A), .LD(d_ff_3_q),
    .O_SR(shft_1_o_sr), .O_SL(shft_1_o_sl), .o(O_A));
  // Probe on shft_1_o_sl
  cnt7 cnt7_1 (.CLK(c6), .RST(RST), .CNT7(cnt7));
  // Probe on O_A
  and and_4 (and_4_out, r_shft, CLk);
  D_FF d_ff_4 (.D(c3), .C(~CLk), .Q(d_ff_4_q));  // open: nQ
  assign driver_1_out = c2 ? inbus : 8'bz;  // Driver driver_1
  // Probe on driver_1_out
  Register #(.Bits(8)) M (.D(driver_1_out), .C(~CLk), .en(c2), .Q(M_q));
  assign xor_1_out = {8{c4}} ^ M_q;  // XOr xor_1, 8 bits wide
  SHFT shft_2 (
    .CLK(CLk), .DIR(dir), .IN_SR(shft_1_o_sr), .IN_SL(1'b0), .RST(and_4_out), .IN(Q), .LD(d_ff_4_q),
    .O_SR(O_SR), .O_SL(shft_2_o_sl), .o(O_Q));
  // Probe on M_q
  // Probe on O_Q
  RCA8 Parallel_Adder (.c_in(c4), .Y(xor_1_out), .X(Q), .Z(Parallel_Adder_z));  // open: c_out
  assign outbus = c3 ? Parallel_Adder_z : 8'bz;  // Driver driver_2

  // Other names for the same wires on the sheet: A_7 = A[7]; Q_0 = Q[0]
endmodule
