// Digital circuit D_FF.dig as structural Verilog
module D_FF (
  input  D,
  input  CLK,
  output Q,
  output nQ
);

  wire nand_1_out, nand_2_out;

  nand nand_1 (nand_1_out, D, CLK);
  nand nand_2 (nand_2_out, ~D, CLK);  // NAnd
  nand nand_3 (Q, nand_1_out, nQ);
  nand nand_4 (nQ, Q, nand_2_out);
endmodule
