// Digital circuit SHFT.dig as structural Verilog
module SHFT (
  input  CLK,
  input  DIR,
  input  IN_SR,
  input  IN_SL,
  output O_SR
);

  wire d_ff_1_q, d_ff_2_q, d_ff_3_q, d_ff_4_q, d_ff_5_q, d_ff_6_q, d_ff_7_q, multiplexer_1_out,
       multiplexer_2_out, multiplexer_3_out, multiplexer_4_out, multiplexer_5_out, multiplexer_6_out,
       multiplexer_7_out, multiplexer_8_out, not_1_out, not_2_out, not_3_out, not_4_out;

  Multiplexer multiplexer_1 (.sel(DIR), .in_0(IN_SR), .in_1(d_ff_2_q), .out(multiplexer_1_out));
  D_FF d_ff_1 (.D(multiplexer_1_out), .CLK(CLK), .Q(d_ff_1_q));  // open: nQ
  Multiplexer multiplexer_2 (.sel(DIR), .in_0(d_ff_1_q), .in_1(d_ff_3_q), .out(multiplexer_2_out));
  not not_1 (not_1_out, CLK);
  D_FF d_ff_2 (.D(multiplexer_2_out), .CLK(not_1_out), .Q(d_ff_2_q));  // open: nQ
  Multiplexer multiplexer_3 (.sel(DIR), .in_0(d_ff_2_q), .in_1(d_ff_4_q), .out(multiplexer_3_out));
  D_FF d_ff_3 (.D(multiplexer_3_out), .CLK(CLK), .Q(d_ff_3_q));  // open: nQ
  Multiplexer multiplexer_4 (.sel(DIR), .in_0(d_ff_3_q), .in_1(d_ff_5_q), .out(multiplexer_4_out));
  not not_2 (not_2_out, CLK);
  D_FF d_ff_4 (.D(multiplexer_4_out), .CLK(not_2_out), .Q(d_ff_4_q));  // open: nQ
  Multiplexer multiplexer_5 (.sel(DIR), .in_0(d_ff_4_q), .in_1(d_ff_6_q), .out(multiplexer_5_out));
  D_FF d_ff_5 (.D(multiplexer_5_out), .CLK(CLK), .Q(d_ff_5_q));  // open: nQ
  Multiplexer multiplexer_6 (.sel(DIR), .in_0(d_ff_5_q), .in_1(d_ff_7_q), .out(multiplexer_6_out));
  not not_3 (not_3_out, CLK);
  D_FF d_ff_6 (.D(multiplexer_6_out), .CLK(not_3_out), .Q(d_ff_6_q));  // open: nQ
  Multiplexer multiplexer_7 (.sel(DIR), .in_0(d_ff_6_q), .in_1(O_SR), .out(multiplexer_7_out));
  D_FF d_ff_7 (.D(multiplexer_7_out), .CLK(CLK), .Q(d_ff_7_q));  // open: nQ
  Multiplexer multiplexer_8 (.sel(DIR), .in_0(d_ff_7_q), .in_1(IN_SL), .out(multiplexer_8_out));
  D_FF d_ff_8 (.D(multiplexer_8_out), .CLK(not_4_out), .Q(O_SR));  // open: nQ
  not not_4 (not_4_out, CLK);
endmodule
