// Digital circuit counter3.dig as structural Verilog
module counter3 (
  input  CNT,
  input  CLK,
  input  RST,
  output [2:0] OUT
);

  wire jk_ff_as_1_nq, jk_ff_as_2_nq;

  JK_FF_AS jk_ff_as_1 (.Set(1'b0), .J(CNT), .C(CLK), .K(CNT), .Clr(RST), .Q(OUT[0]), .nQ(jk_ff_as_1_nq));
  JK_FF_AS jk_ff_as_2 (.Set(1'b0), .J(CNT), .C(jk_ff_as_1_nq), .K(CNT), .Clr(RST), .Q(OUT[1]), .nQ(jk_ff_as_2_nq));
  JK_FF_AS jk_ff_as_3 (.Set(1'b0), .J(CNT), .C(jk_ff_as_2_nq), .K(CNT), .Clr(RST), .Q(OUT[2]));  // open: nQ

  // Other names for the same wires on the sheet: J = CNT
endmodule
