// Digital circuit ALU.dig as structural Verilog
module ALU (
  input  [7:0] inbus,
  input  [1:0] op,
  input  CLk,
  input  Begin,
  input  RST,
  output [7:0] outbus
);

  wire A_7, c0, c0_t, c1, c2, c3, c4, c5, c6, c7, c7_5, c8, cL, cnt7, cR, d_ff_1_q, d_ff_3_q, L, LA, LQ,
       multiplexer_4_out, not_1_out, O_SR, or_1_out, or_10_out, Q__1, shf2_1_o_sl, shf2_1_o_sr, shf2_2_o_sl,
       shf2_2_o_sr, shft;
  wire [0:0] and_4_out;
  wire [1:0] or_4_out, or_8_out;
  wire [3:0] counter_1_out;
  wire [6:0] O_A;
  wire [7:0] add, and_2_out, and_3_out, driver_1_out, in, inA, inQ, M_q, O_Q, xor_1_out;

  D_FF d_ff_1 (.D(shft), .C(CLk), .Q(d_ff_1_q));  // open: nQ
  or or_1 (or_1_out, c0, c0_t);
  or or_2 (or_4_out[1], d_ff_1_q, c3);
  or or_3 (shft, cL, cR);
  or or_4 (or_4_out[0], or_1_out, c3);
  and and_1 (L, ~cR, ~cL);  // And
  assign and_2_out = add & {8{c3}};  // And and_2, 8 bits wide
  assign and_3_out = ~{8{c3}} & {A_7, O_A};  // And and_3, 8 bits wide
  // Probe on O_A
  assign in = and_2_out | and_3_out;  // Or or_5, 8 bits wide
  // Probe on inA
  or or_6 (LA, c0, c0_t, c3, d_ff_1_q);
  Multiplexer #(.Selector_Bits(2), .Bits(8)) multiplexer_1 (
    .sel(or_4_out), .in_0({A_7, O_A}), .in_1(inbus), .in_2({A_7, O_A}), .in_3(add), .out(inA));
  shf2 shf2_1 (
    .CLK(CLk), .SR(cR), .SL(cL), .IN_SR(A_7), .IN_SL(shf2_2_o_sl), .IN(inA), .LD(L), .O_sr(shf2_1_o_sr),
    .O_sl(shf2_1_o_sl), .O({A_7, O_A}));
  // Probe on shf2_1_o_sl
  // Probe on {A_7, O_A}
  not not_1 (not_1_out, A_7);
  shf2 shf2_2 (
    .CLK(CLk), .SR(cR), .SL(cL), .IN_SR(shf2_1_o_sr), .IN_SL(not_1_out), .IN(inQ), .LD(L),
    .O_sr(shf2_2_o_sr), .O_sl(shf2_2_o_sl), .O(O_Q));
  D_FF d_ff_2 (.D(shf2_2_o_sr), .C(CLk), .Q(O_SR));  // open: nQ
  // Probe on O_Q
  ALU_CU alu_cu_1 (
    .BGN(Begin), .RST(RST), .CLK(CLk), .CNT7(cnt7), .Q0(O_Q[0]), .Q_1(Q__1), .A7(A_7), .OP(op), .c0(c0),
    .c0_2(c0_t), .c1(c1), .c2(c2), .c3(c3), .c4(c4), .cR(cR), .cL(cL), .c5(c5), .c7(c7), .c8(c8), .c6(c6),
    .c7_5(c7_5));
  and and_4 (and_4_out[0], ~c7_5, ~A_7, c5);  // And
  // Probe on O_Q[0]
  or or_7 (or_8_out[0], c1, c5);
  D_FF d_ff_3 (.D(shft), .C(CLk), .Q(d_ff_3_q));  // open: nQ
  or or_8 (or_8_out[1], c5, d_ff_3_q);
  // Probe on inQ
  or or_9 (LQ, c1, c5, d_ff_3_q);
  Multiplexer #(.Selector_Bits(2), .Bits(8)) multiplexer_2 (
    .sel(or_8_out), .in_0(O_Q), .in_1(inbus), .in_2(O_Q), .in_3({O_Q[7:1], and_4_out[0]}), .out(inQ));
  Multiplexer #(.Selector_Bits(2), .Bits(8)) multiplexer_3 (
    .sel({c8, c7}), .in_0({8{1'b0}}), .in_1(O_Q), .in_2({A_7, O_A}), .in_3({8{1'b0}}), .out(outbus));
  Multiplexer multiplexer_4 (.sel(or_10_out), .in_0(Q__1), .in_1(O_SR), .out(multiplexer_4_out));
  or or_10 (or_10_out, c1, d_ff_3_q);
  Counter #(.Bits(4)) counter_1 (.en(c6), .C(CLk), .clr(RST), .out(counter_1_out));  // open: ovf
  // Probe on O_Q[0]
  D_FF d_ff_4 (.D(multiplexer_4_out), .CLK(CLk), .R(RST), .Q(Q__1));  // open: nQ
  // Probe on O_Q[7:1]
  // Probe on O_Q
  // Probe on Q__1
  and and_5 (cnt7, ~counter_1_out[0], ~counter_1_out[1], ~counter_1_out[2], counter_1_out[3]);  // And
  assign driver_1_out = c2 ? inbus : 8'bz;  // Driver driver_1
  // Probe on driver_1_out
  Register #(.Bits(8)) M (.D(driver_1_out), .C(CLk), .en(c2), .Q(M_q));
  assign xor_1_out = {8{c4}} ^ M_q;  // XOr xor_1, 8 bits wide
  // Probe on M_q
  RCA8 Parallel_Adder (.c_in(c4), .Y(xor_1_out), .X({A_7, O_A}), .Z(add));  // open: c_out

  // Other names for the same wires on the sheet: O_A[7] = A_7; Q_0 = O_Q[0]
endmodule
